// Logisim project u16a.circ as structural Verilog: 1 circuit, main circuit main
module main (
);

  wire ADDR_WRITE, ALU_F, ALU_NO, ALU_NX, ALU_NY, ALU_OUT_NEG, ALU_OUT_ZERO, ALU_READ, ALU_ZX, ALU_ZY,
       and_1_out, and_2_out, and_3_out, and_4_out, and_5_out, and_6_out, and_7_out, BX_READ, BX_WRITE,
       BY_READ, BY_WRITE, CLK, decoder_1_out6, decoder_1_out7, decoder_2_out7, demultiplexer_1_out0,
       demultiplexer_1_out1, INST_STEP_RESET, INST_WRITE, INV_CLK, IP_COUNT, IP_READ, IP_WRITE, not_2_out,
       RAM_READ, RAM_WRITE;
  wire [3:0] ADDR_q;
  wire [6:0] INST_STEP_q, multiplexer_6_out;
  wire [7:0] adder_1_out, ALU_IN_X, ALU_IN_Y, and_8_out, DBUS, dipswitch_1_sw8, INST_q, IP_q,
       multiplexer_1_out, multiplexer_2_out, multiplexer_3_out, multiplexer_4_out, multiplexer_5_out,
       not_3_out, not_4_out, not_5_out, ram_1_dout, register_1_q, register_2_q;
  wire [7:4] ADDR_q_2;
  wire [13:0] MICROINSTRUCTIONS_data;

  Counter IP (.clr(1'b0), .load(IP_WRITE), .up(1'b1), .count(IP_COUNT), .clk(CLK), .D(DBUS), .Q(IP_q));  // open: carry
  Register BX (.D(DBUS), .en(BX_WRITE), .clk(CLK), .Q(ALU_IN_X));  // open: clr
  Register BY (.D(DBUS), .en(BY_WRITE), .clk(CLK), .Q(ALU_IN_Y));  // open: clr
  assign DBUS = IP_READ ? IP_q : 8'bz;  // Controlled_Buffer controlled_buffer_1
  assign DBUS = BX_READ ? ALU_IN_X : 8'bz;  // Controlled_Buffer controlled_buffer_2
  assign DBUS = BY_READ ? ALU_IN_Y : 8'bz;  // Controlled_Buffer controlled_buffer_3
  Register ADDR (.D(DBUS), .en(ADDR_WRITE), .clk(CLK), .Q({ADDR_q_2, ADDR_q}));  // open: clr
  Counter #(.max('h7f), .width(7)) INST_STEP (
    .clr(INST_STEP_RESET), .load(1'b0), .up(1'b1), .count(1'b1), .clk(INV_CLK), .Q(INST_STEP_q));  // open: D, carry
  Clock clock_1 (.out(CLK));
  and and_1 (and_1_out, ADDR_q_2[7], ADDR_q_2[6], ADDR_q_2[5], ADDR_q_2[4]);
  and and_2 (and_2_out, and_1_out, demultiplexer_1_out0);
  and and_3 (and_3_out, and_1_out, demultiplexer_1_out1);
  Demultiplexer #(.select(4)) demultiplexer_1 (
    .out0(demultiplexer_1_out0), .out1(demultiplexer_1_out1), .in(1'b1), .sel(ADDR_q));  // open: out2, out3, out4, out5, out6, out7, out8, out9, out10, out11, out12, out13, out14, out15
  not not_1 (INV_CLK, CLK);
  not not_2 (not_2_out, and_1_out);
  DipSwitch dipswitch_1 (
    .sw1(dipswitch_1_sw8[7]), .sw2(dipswitch_1_sw8[6]), .sw3(dipswitch_1_sw8[5]), .sw4(dipswitch_1_sw8[4]),
    .sw5(dipswitch_1_sw8[3]), .sw6(dipswitch_1_sw8[2]), .sw7(dipswitch_1_sw8[1]), .sw8(dipswitch_1_sw8[0]));
  Register INST (.D(DBUS), .en(INST_WRITE), .clk(CLK), .Q(INST_q));  // open: clr
  and and_4 (and_4_out, RAM_WRITE, not_2_out);
  and and_5 (and_5_out, RAM_WRITE, and_2_out);
  ROM #(.addrWidth(16), .dataWidth(16)) MICROINSTRUCTIONS (
    .addr({INST_q, INST_STEP_q, ALU_OUT_ZERO}),
    .data({INST_STEP_RESET, IP_COUNT, MICROINSTRUCTIONS_data[13:8], ALU_NO, ALU_F, ALU_NY, ALU_ZY, ALU_NX, ALU_ZX, MICROINSTRUCTIONS_data[1:0]}));
  RAM #(.asyncread("true"), .\type ("nonvolatile")) ram_1 (
    .addr({ADDR_q_2, ADDR_q}), .we(and_4_out), .oe(1'b1), .clk(CLK), .din(DBUS), .dout(ram_1_dout));
  Register register_1 (.D(DBUS), .en(and_5_out), .clk(CLK), .Q(register_1_q));  // open: clr
  Register register_2 (.D(dipswitch_1_sw8), .en(1'b1), .clk(CLK), .Q(register_2_q));  // open: clr
  and and_6 (and_6_out, RAM_READ, and_3_out);
  assign DBUS = and_6_out ? register_2_q : 8'bz;  // Controlled_Buffer controlled_buffer_4
  // Probe on {INST_STEP_RESET, IP_COUNT, MICROINSTRUCTIONS_data[13:8], ALU_NO, ALU_F, ALU_NY, ALU_ZY, ALU_NX, ALU_ZX, MICROINSTRUCTIONS_data[1:0]}
  assign DBUS = and_7_out ? ram_1_dout : 8'bz;  // Controlled_Buffer controlled_buffer_5
  and and_7 (and_7_out, RAM_READ, not_2_out);
  Decoder #(.enable("false"), .select(3)) decoder_1 (
    .out1(RAM_READ), .out2(IP_READ), .out3(BX_READ), .out4(BY_READ), .out5(ALU_READ), .out6(decoder_1_out6),
    .out7(decoder_1_out7), .sel(MICROINSTRUCTIONS_data[10:8]));  // open: out0
  Decoder #(.enable("false"), .select(3)) decoder_2 (
    .out1(ADDR_WRITE), .out2(INST_WRITE), .out3(IP_WRITE), .out4(BX_WRITE), .out5(BY_WRITE),
    .out6(RAM_WRITE), .out7(decoder_2_out7), .sel(MICROINSTRUCTIONS_data[13:11]));  // open: out0
  Multiplexer #(.width(8)) multiplexer_1 (.in0(ALU_IN_X), .in1({8{1'b0}}), .out(multiplexer_1_out), .sel(ALU_ZX));
  Multiplexer #(.width(8)) multiplexer_2 (.in0(ALU_IN_Y), .in1({8{1'b0}}), .out(multiplexer_2_out), .sel(ALU_ZY));
  Multiplexer #(.width(8)) multiplexer_3 (
    .in0(multiplexer_1_out), .in1(not_3_out), .out(multiplexer_3_out), .sel(ALU_NX));
  assign not_3_out = ~multiplexer_1_out;  // NOT_Gate not_3, 8 bits wide
  Multiplexer #(.width(8)) multiplexer_4 (
    .in0(multiplexer_2_out), .in1(not_4_out), .out(multiplexer_4_out), .sel(ALU_NY));
  assign not_4_out = ~multiplexer_2_out;  // NOT_Gate not_4, 8 bits wide
  assign and_8_out = multiplexer_3_out & multiplexer_4_out;  // AND_Gate and_8, 8 bits wide
  Adder adder_1 (.a(multiplexer_3_out), .b(multiplexer_4_out), .out(adder_1_out), .cin(1'b0));  // open: cout
  Multiplexer #(.width(8)) multiplexer_5 (.in0(and_8_out), .in1(adder_1_out), .out(multiplexer_5_out), .sel(ALU_F));
  assign not_5_out = ~multiplexer_5_out;  // NOT_Gate not_5, 8 bits wide
  Hex_Digit_Display hex_digit_display_1 (.value(register_1_q[7:4]));  // open: dp
  Hex_Digit_Display hex_digit_display_2 (.value(register_1_q[3:0]));  // open: dp
  Multiplexer #(.width(8)) multiplexer_6 (
    .in0(multiplexer_5_out), .in1(not_5_out), .out({ALU_OUT_NEG, multiplexer_6_out}), .sel(ALU_NO));
  assign DBUS = ALU_READ ? {ALU_OUT_NEG, multiplexer_6_out} : 8'bz;  // Controlled_Buffer controlled_buffer_6
  nor nor_1 (ALU_OUT_ZERO, multiplexer_6_out[0], multiplexer_6_out[1], multiplexer_6_out[2], multiplexer_6_out[3], multiplexer_6_out[4], multiplexer_6_out[5], multiplexer_6_out[6], ALU_OUT_NEG);

  // Notes on the sheet:
  //   contents of MICROINSTRUCTIONS (hex, n*v repeats v):
  //   a00 a00 5100 5100 8000 8000 250*0 a00 a00 5100 5100 a00 a00 5900 5900 8000 8000 246*0 a00 a00 5100
  //   5100 25f8 25f8 8000 8000 248*0 a00 a00 5100 5100 2570 2570 8000 8000 248*0 a00 a00 5100 5100 a00 a00
  //   6100 6100 8000 8000 246*0 a00 a00 5100 5100 a00 a00 4900 4900 3300 3300 8000 8000 244*0 a00 a00 5100
  //   5100 a00 a00 4900 4900 2100 2100 8000 8000 244*0 a00 a00 5100 5100 a30 a30 4030 5930 8000 8000 246*0
  //   a00 a00 5100 5100 25ec 25ec 8000 8000 248*0 a00 a00 5100 5100 254c 254c 8000 8000 248*0 a00 a00 5100
  //   5100 a00 a00 6100 6100 8000 8000 246*0 a00 a00 5100 5100 a00 a00 4900 4900 3400 3400 8000 8000 244*0
  //   a00 a00 5100 5100 a00 a00 4900 4900 2900 2900 8000 8000 244*0 a00 a00 5100 5100 a0c a0c 400c 590c
  //   8000 8000
endmodule
